# Fritzing sketch BlueCar (saved by Fritzing 0.9.9b)

parts:
  L298N2 = L298N DC motor driver
  Parça1 = Arduino Uno (Rev3) - ICSP
  VCC1 = Battery block 9V  # not connected
  M1 = DC Motor  # not connected
  M2 = DC Motor  # not connected
  M3 = DC Motor  # not connected
  M4 = DC Motor  # not connected
  Parça2 = Bluetooth HC-05 Macho
  J1 = Piezo Speaker
  LED1 = LED - 5mm [color="Red (633nm)" current=0.030 package="5 mm [THT]"]
  HC-SR04_Sensor_1 = HC-SR04 Ultrasonic Distance Sensor

nets:
  N1: L298N2.IN1, Parça1.A3
  N2: L298N2.IN2, Parça1.A2
  N3: L298N2.IN3, Parça1.A1
  N4: L298N2.IN4, Parça1.A0
  N5: Parça1.D8, LED1.anode
  N6: Parça1.D9_PWM, J1.pin2
  N7: Parça1.D10_PWM/SS, HC-SR04_Sensor_1.ECHO
  N8: Parça1.D11_PWM/MOSI, HC-SR04_Sensor_1.TRIG
  GND: Parça1.GND, Parça2.GND, LED1.cathode, HC-SR04_Sensor_1.GND
  N9: Parça1.D0/RX, Parça2.TXD
  N10: Parça1.D1/TX, Parça2.RXD
  3V3: Parça1.3V3, HC-SR04_Sensor_1.VCC
  5V: Parça1.5V, Parça2.VCC

custom parts:
  L298N DC motor driver: 2x DC motor driver with 78M05 positive voltage regulator (7..35 V) L298N: max 46 V, 2 A Set 5 V Enable jumper to enable 5 V regultor (needed for the L298N) and +5 V output at screw terminal or supply external +5 V at screw terminal Set ENA and/or ENB to +5 V to enable motor permanently or supply ENA and/or ENB with PWM signal IN1 and IN2 set rotation directory for motor A (OUT1/OUT2) IN2 and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
